// Digital circuit Lab02.dig as structural Verilog
module Lab02 (
  input  B,
  input  C,
  input  A,
  input  D,
  output Fa,
  output Fb,
  output Fc,
  output Fd,
  output Fe,
  output Fg,
  output Ff
);

  wire and_1_out, and_2_out, and_3_out, and_4_out, and_5_out, and_6_out, Fb_t, Fc_t, Fd_t, Fe_t, Ff_t, Fg_t,
       not_1_out, not_2_out, not_3_out, not_4_out, not_5_out, not_6_out, not_7_out, or_1_out, or_2_out,
       or_3_out;

  and and_1 (and_1_out, B, C);
  and and_2 (and_2_out, A, not_1_out);
  not not_1 (not_1_out, D);
  and and_3 (and_3_out, not_2_out, C);
  not not_2 (not_2_out, A);
  and and_4 (and_4_out, not_3_out, not_4_out);
  not not_3 (not_3_out, B);
  not not_4 (not_4_out, D);
  and and_5 (and_5_out, not_5_out, B, D);
  not not_5 (not_5_out, A);
  and and_6 (and_6_out, A, not_6_out, not_7_out);
  not not_6 (not_6_out, B);
  not not_7 (not_7_out, C);
  or or_1 (or_1_out, and_1_out, and_2_out);
  or or_2 (or_2_out, and_3_out, and_4_out);
  or or_3 (or_3_out, and_5_out, and_6_out);
  or or_4 (Fa, or_1_out, or_2_out, or_3_out);
  Seven_Seg seven_seg_1 (.a(Fa), .b(Fb_t), .c(Fc_t), .d(Fd_t), .e(Fe_t), .f(Ff_t), .g(Fg_t), .dp(1'b0));
endmodule
